# Fritzing sketch Relay_Unit (saved by Fritzing 0.9.3b)
circuit board: 8.46667cm x 5.64444cm

parts:
  U1 = RELAY [package=relay-jzc]
  U2 = RELAY [package=relay-jzc]
  U3 = RELAY [part_number=BombaUV package=relay-jzc]
  U4 = RELAY [package=relay-jzc]
  U5 = RELAY [package=relay-jzc]
  U6 = RELAY [package=relay-jzc]
  U9 = Molex Picoblade Series Header [part_number=0532610219 package=Picoblade-53261-0219]
  U10 = Molex Picoblade Series Header [part_number=0532610219 package=Picoblade-53261-0219]
  U11 = Molex Picoblade Series Header [part_number=0532610219 package=Picoblade-53261-0219]
  U12 = Molex Picoblade Series Header [part_number=0532610219 package=Picoblade-53261-0219]
  U13 = Molex Picoblade Series Header [part_number=0532610219 package=Picoblade-53261-0219]
  U14 = Molex Picoblade Series Header [part_number=0532610219 package=Picoblade-53261-0219]
  V1 = DC Power [voltage=5]
  J4 = male pin header, 1 pin [form="♂ (male)"]

nets:
  N1: U1.NO, U10.2
  N2: U1.MAIN, U10.1
  N3: U2.NO, U9.2
  N4: U2.MAIN, U9.1
  N5: U3.NO, U11.2
  N6: U3.MAIN, U4.MAIN, U5.MAIN, V1.V+, J4.pin1
  N7: U4.NO, U12.2
  N8: U5.NO, U13.2
  N9: U6.NC, U14.1
  N10: U6.MAIN, U14.2
  N11: U11.1, U12.1, U13.1, V1.V-

notes:
  Filtro
  Inversor
  UV
  BombaUV
  BombaPozo
  Voltaje
  Amperemeter
  Voltage Regulator (12)
