# Fritzing sketch Solar_Input (saved by Fritzing 0.9.5d)

parts:
  V1 = DC Power [voltage=12V]
  V2 = DC Power [voltage=19]
  U1 = RELAY [package=relay-t9a-2]
  J2 = male pin header, 1 pin [form="♂ (male)"]
  U2 = RELAY [package=relay-t9a-2]

nets:
  N1: V1.V+, V2.V+, V2.V-, U1.NC, J2.pin1, U2.NO
  N2: V1.V-, U1.MAIN, U2.MAIN

notes:
  Voltmeter
  Voltage regulator (12v)
  Volt relay
  Volt SR
  Solar Panel
