# Fritzing sketch Fan_Module (saved by Fritzing 0.9.3b)
breadboards: 1

parts:
  Power_plug1 = Power plug [part_number=12V]
  Componente1 = Arduino Uno (Rev3) - ICSP
  Q4 = Basic FET N-Channel [package="TO220 [THT]"]
  Q5 = Basic FET N-Channel [package="TO220 [THT]"]
  Q6 = Basic FET N-Channel [package="TO220 [THT]"]
  M1 = DC Motor
  M2 = DC Motor
  M3 = DC Motor

nets:
  GND: Power_plug1.GND, Componente1.GND, Q4.source, Q5.source, Q6.source
  N1: Power_plug1.VCC, M1.pin_1, M2.pin_1, M3.pin_1
  N2: Componente1.D3_PWM, Q4.gate
  N3: Componente1.D5_PWM, Q5.gate
  N4: Componente1.D6_PWM, Q6.gate
  N5: Q4.drain, M2.pin_2
  N6: Q5.drain, M3.pin_2
  N7: Q6.drain, M1.pin_2
